// Logisim project CPU.circ as structural Verilog: 2 circuits, main circuit main
module main (
);

  wire alu_1_f_out, BOOTSTRAPPING, CLK, CLK_RAW, FAULT, FAULTED, FLAG_BUS, HALT, HALTED, INSN_END, JMP,
       LOAD_A, LOAD_ALU, LOAD_B, LOAD_INTERNAL_A, LOAD_PROG, not_1_out, PROG_NEXT, pull_resistor_1_node,
       pull_resistor_2_node, PWR, RESET, STORE_A, STORE_ALU_OP, STORE_B, STORE_DISPLAY, STORE_INSN,
       STORE_INTERNAL_A, ZERO_FAULT, ZERO_FAULTED;
  wire [1:0] pull_resistor_6_node;
  wire [3:0] bitselector_1_out;
  wire [5:0] bitadder_1_out;
  wire [7:0] pull_resistor_3_node, STEP;
  wire [15:0] alu_1_out, BUS, DISPLAY, INSN, PROG_ADDR, REG_A, REG_B, register_1_q, register_2_q,
       register_6_q, rom_1_data;
  wire [31:15] rom_2_data;

  LED led_1 (.in(PWR));
  D_Flip_Flop #(.trigger("falling")) d_ff_1 (.D(HALT), .clk(CLK), .Q(HALTED), .reset(RESET));  // open: Qn, preset
  D_Flip_Flop #(.trigger("falling")) d_ff_2 (.D(FAULT), .clk(CLK), .Q(FAULTED), .reset(RESET));  // open: Qn, preset
  D_Flip_Flop #(.trigger("falling")) d_ff_3 (
    .D(ZERO_FAULT), .clk(CLK), .Q(ZERO_FAULTED), .reset(RESET));  // open: Qn, preset
  ROM #(.addrWidth(16), .dataWidth(16)) rom_1 (.addr(PROG_ADDR), .data(rom_1_data));
  Pull_Resistor #(.pull(1)) pull_resistor_1 (.node(pull_resistor_1_node));
  Pull_Resistor #(.pull(1)) pull_resistor_2 (.node(pull_resistor_2_node));
  Pull_Resistor pull_resistor_3 (.node(pull_resistor_3_node));
  Clock clock_1 (.out(CLK_RAW));
  Button button_1 (.out(RESET));
  // Probe on DISPLAY
  Counter #(.width(16), .max('hffff)) counter_1 (
    .clr(RESET), .load(JMP), .up(pull_resistor_1_node), .count(PROG_NEXT), .clk(CLK), .D(BUS), .Q(PROG_ADDR));  // open: carry
  Register #(.width(16)) register_1 (.D(BUS), .en(STORE_INSN), .clk(CLK), .Q(register_1_q), .clr(RESET));
  Counter counter_2 (
    .clr(RESET), .load(INSN_END), .up(pull_resistor_2_node), .clk(CLK), .D(pull_resistor_3_node), .Q(STEP));  // open: count, carry
  // Probe on DISPLAY
  // Probe on BUS
  D_Flip_Flop d_ff_4 (.D(1'b1), .clk(CLK), .Qn(BOOTSTRAPPING), .reset(RESET));  // open: Q, preset
  // Probe on DISPLAY
  LED led_2 (.in(FAULTED));
  LED led_3 (.in(ZERO_FAULTED));
  not not_1 (not_1_out, BOOTSTRAPPING);
  assign INSN = not_1_out ? register_1_q : 16'bz;  // Controlled_Buffer controlled_buffer_1
  assign INSN = BOOTSTRAPPING ? {16{1'b1}} : 16'bz;  // Controlled_Buffer controlled_buffer_2
  assign CLK = PWR ? CLK_RAW : 1'bz;  // Controlled_Buffer controlled_buffer_3
  Pull_Resistor pull_resistor_4 (.node(CLK));
  Pull_Resistor pull_resistor_5 (.node(LOAD_PROG));
  assign BUS = LOAD_PROG ? rom_1_data : 16'bz;  // Controlled_Buffer controlled_buffer_4
  nor nor_1 (PWR, HALTED, ZERO_FAULTED, FAULTED);
  ROM #(.addrWidth(24), .dataWidth(32)) rom_2 (
    .addr({INSN, STEP}),
    .data({rom_2_data, STORE_INTERNAL_A, STORE_ALU_OP, STORE_DISPLAY, STORE_INSN, STORE_B, STORE_A, LOAD_INTERNAL_A, LOAD_ALU, LOAD_B, LOAD_A, FAULT, HALT, LOAD_PROG, PROG_NEXT, INSN_END}));
  Register #(.width(16)) register_2 (.D(BUS), .en(STORE_ALU_OP), .clk(CLK), .Q(register_2_q), .clr(RESET));
  Register #(.width(16)) register_3 (.D(BUS), .en(STORE_A), .clk(CLK), .Q(REG_A), .clr(RESET));
  Register #(.width(16)) register_4 (.D(BUS), .en(STORE_B), .clk(CLK), .Q(REG_B), .clr(RESET));
  Register #(.width(16)) register_5 (.D(BUS), .en(STORE_DISPLAY), .clk(CLK), .Q(DISPLAY), .clr(RESET));
  Register #(.width(16)) register_6 (.D(BUS), .en(STORE_INTERNAL_A), .clk(CLK), .Q(register_6_q), .clr(RESET));
  Pull_Resistor pull_resistor_6 (.node(pull_resistor_6_node));
  LED led_4 (.in(CLK));
  assign BUS = LOAD_A ? REG_A : 16'bz;  // Controlled_Buffer controlled_buffer_5
  Pull_Resistor pull_resistor_7 (.node(LOAD_A));
  assign BUS = LOAD_B ? REG_B : 16'bz;  // Controlled_Buffer controlled_buffer_6
  Pull_Resistor pull_resistor_8 (.node(LOAD_B));
  assign BUS = LOAD_INTERNAL_A ? register_6_q : 16'bz;  // Controlled_Buffer controlled_buffer_7
  Pull_Resistor pull_resistor_9 (.node(LOAD_INTERNAL_A));
  BitSelector #(.width(16), .group(4)) bitselector_1 (
    .in(register_2_q), .out(bitselector_1_out), .sel(pull_resistor_6_node));
  ALU alu_1 (.OP(bitselector_1_out), .A(REG_A), .B(REG_B), .OUT(alu_1_out), .F_OUT(alu_1_f_out));
  Pull_Resistor pull_resistor_10 (.node(LOAD_ALU));
  Pull_Resistor pull_resistor_11 (.node({rom_2_data, STORE_INTERNAL_A, STORE_ALU_OP, STORE_DISPLAY, STORE_INSN, STORE_B, STORE_A, LOAD_INTERNAL_A, LOAD_ALU, LOAD_B, LOAD_A, FAULT, HALT, LOAD_PROG, PROG_NEXT, INSN_END}));
  LED led_5 (.in(CLK));
  assign BUS = LOAD_ALU ? alu_1_out : 16'bz;  // Controlled_Buffer controlled_buffer_8
  assign FLAG_BUS = LOAD_ALU ? alu_1_f_out : 1'bz;  // Controlled_Buffer controlled_buffer_9
  BitAdder #(.width(32)) bitadder_1 (
    .in0({rom_2_data, STORE_INTERNAL_A, STORE_ALU_OP, STORE_DISPLAY, STORE_INSN, STORE_B, STORE_A, LOAD_INTERNAL_A, LOAD_ALU, LOAD_B, LOAD_A, FAULT, HALT, LOAD_PROG, PROG_NEXT, INSN_END}),
    .out(bitadder_1_out));
  nor nor_2 (ZERO_FAULT, bitadder_1_out[5], bitadder_1_out[4], bitadder_1_out[3], bitadder_1_out[2], bitadder_1_out[1], bitadder_1_out[0]);

  // Notes on the sheet:
  //   contents of rom_1 (hex, n*v repeats v):
  //   130 6 131 7 22 2
  //   Halt
  //   Fault
  //   Zero Fault
  //   Program ROM
  //   Program Counter
  //   Instruction register
  //   Step Counter
  //   Normal
  //   BUS
  //   DISPLAY
  //   FAULT
  //   Microcode == 0
  //   contents of rom_2 (hex, n*v repeats v):
  //   8 807 254*0 807 7935*0 1020 807 254*0 1040 807 254*0 2006 1080 807 253*0 1006 807 56574*0 220 807
  //   254*0 420 807 3838*0 240 807 254*0 440 807 3838*0 2006 280 807 253*0 2006 480 807 3837*0 206 807
  //   254*0 406 807 16698878*0 807
  //   Microcode
  //   ALU
  //   Registers
  //   Display
  //   Internal Registers (for use by microcode only)
endmodule

module ALU (
  input  [3:0] OP,
  input  [15:0] A,
  input  [15:0] B,
  output [15:0] OUT,
  output F_OUT
);

  wire comparator_1_eq, comparator_1_gt, comparator_1_lt, decoder_1_out0, decoder_1_out1, decoder_1_out2,
       decoder_1_out3, decoder_1_out4, decoder_1_out5, decoder_1_out6, decoder_1_out7, decoder_1_out8,
       decoder_1_out9, decoder_1_out10, decoder_1_out11, decoder_1_out12, decoder_1_out13, decoder_1_out14,
       decoder_1_out15, pull_resistor_5_node, pull_resistor_6_node;
  wire [1:0] pull_resistor_3_node, pull_resistor_4_node;
  wire [3:0] bitselector_1_out, bitselector_2_out;
  wire [4:0] bitadder_1_out;
  wire [15:0] adder_1_out, and_1_out, bit_extender_1_out, divider_1_out, multiplier_1_out, negator_1_out,
       not_1_out, or_1_out, pull_resistor_7_node, pull_resistor_8_node, shifter_1_out, shifter_2_out,
       subtractor_1_out, xor_1_out;

  Pull_Resistor pull_resistor_1 (.node(A));
  Pull_Resistor pull_resistor_2 (.node(B));
  Pull_Resistor pull_resistor_3 (.node(pull_resistor_3_node));
  Pull_Resistor pull_resistor_4 (.node(pull_resistor_4_node));
  Pull_Resistor pull_resistor_5 (.node(pull_resistor_5_node));
  Pull_Resistor pull_resistor_6 (.node(pull_resistor_6_node));
  Pull_Resistor pull_resistor_7 (.node(pull_resistor_7_node));
  Pull_Resistor pull_resistor_8 (.node(pull_resistor_8_node));
  BitSelector #(.width(16), .group(4)) bitselector_1 (.in(B), .out(bitselector_1_out), .sel(pull_resistor_3_node));
  BitSelector #(.width(16), .group(4)) bitselector_2 (.in(B), .out(bitselector_2_out), .sel(pull_resistor_4_node));
  Adder #(.width(16)) adder_1 (.a(A), .b(B), .out(adder_1_out), .cin(pull_resistor_5_node));  // open: cout
  Subtractor #(.width(16)) subtractor_1 (
    .a(A), .b(B), .out(subtractor_1_out), .bin(pull_resistor_6_node));  // open: bout
  Multiplier #(.width(16)) multiplier_1 (
    .a(A), .b(B), .out(multiplier_1_out), .cin(pull_resistor_7_node));  // open: cout
  Divider #(.width(16)) divider_1 (.a(A), .b(B), .out(divider_1_out), .upper(pull_resistor_8_node));  // open: rem
  Negator #(.width(16)) negator_1 (.in(A), .out(negator_1_out));
  Shifter #(.width(16)) shifter_1 (.in(A), .\dist (bitselector_1_out), .out(shifter_1_out));
  Shifter #(.width(16), .shift("lr")) shifter_2 (.in(A), .\dist (bitselector_2_out), .out(shifter_2_out));
  BitAdder #(.width(16)) bitadder_1 (.in0(A), .out(bitadder_1_out));
  Comparator #(.width(16)) comparator_1 (
    .a(A), .b(B), .gt(comparator_1_gt), .eq(comparator_1_eq), .lt(comparator_1_lt));
  assign not_1_out = ~A;  // NOT_Gate not_1, 16 bits wide
  assign and_1_out = A & B;  // AND_Gate and_1, 16 bits wide
  assign or_1_out = A | B;  // OR_Gate or_1, 16 bits wide
  assign xor_1_out = A ^ B;  // XOR_Gate xor_1, 16 bits wide
  Decoder #(.select(4)) decoder_1 (
    .out0(decoder_1_out0), .out1(decoder_1_out1), .out2(decoder_1_out2), .out3(decoder_1_out3),
    .out4(decoder_1_out4), .out5(decoder_1_out5), .out6(decoder_1_out6), .out7(decoder_1_out7),
    .out8(decoder_1_out8), .out9(decoder_1_out9), .out10(decoder_1_out10), .out11(decoder_1_out11),
    .out12(decoder_1_out12), .out13(decoder_1_out13), .out14(decoder_1_out14), .out15(decoder_1_out15),
    .sel(OP));  // open: en
  Pull_Resistor pull_resistor_9 (.node(OP));
  assign OUT = decoder_1_out0 ? adder_1_out : 16'bz;  // Controlled_Buffer controlled_buffer_1
  assign OUT = decoder_1_out1 ? subtractor_1_out : 16'bz;  // Controlled_Buffer controlled_buffer_2
  assign OUT = decoder_1_out2 ? multiplier_1_out : 16'bz;  // Controlled_Buffer controlled_buffer_3
  assign OUT = decoder_1_out3 ? divider_1_out : 16'bz;  // Controlled_Buffer controlled_buffer_4
  assign OUT = decoder_1_out4 ? negator_1_out : 16'bz;  // Controlled_Buffer controlled_buffer_5
  assign OUT = decoder_1_out5 ? shifter_1_out : 16'bz;  // Controlled_Buffer controlled_buffer_6
  assign OUT = decoder_1_out6 ? shifter_2_out : 16'bz;  // Controlled_Buffer controlled_buffer_7
  assign OUT = decoder_1_out7 ? bit_extender_1_out : 16'bz;  // Controlled_Buffer controlled_buffer_8
  assign bit_extender_1_out = {{11{bitadder_1_out[4]}}, bitadder_1_out};  // Bit_Extender bit_extender_1
  assign F_OUT = decoder_1_out8 ? comparator_1_eq : 1'bz;  // Controlled_Buffer controlled_buffer_9
  assign F_OUT = decoder_1_out9 ? ~comparator_1_eq : 1'bz;  // Controlled_Inverter controlled_inverter_1
  assign F_OUT = decoder_1_out10 ? comparator_1_lt : 1'bz;  // Controlled_Buffer controlled_buffer_10
  assign F_OUT = decoder_1_out11 ? comparator_1_gt : 1'bz;  // Controlled_Buffer controlled_buffer_11
  assign OUT = decoder_1_out12 ? not_1_out : 16'bz;  // Controlled_Buffer controlled_buffer_12
  assign OUT = decoder_1_out13 ? and_1_out : 16'bz;  // Controlled_Buffer controlled_buffer_13
  assign OUT = decoder_1_out14 ? or_1_out : 16'bz;  // Controlled_Buffer controlled_buffer_14
  assign OUT = decoder_1_out15 ? xor_1_out : 16'bz;  // Controlled_Buffer controlled_buffer_15
  Pull_Resistor pull_resistor_10 (.node(OUT));
  Pull_Resistor pull_resistor_11 (.node(F_OUT));

  // Notes on the sheet:
  //   0b0000 - ADD
  //   0b0001 - SUB
  //   0b0010 - MUL
  //   0b0011 - DIV
  //   0b0100 - NEG
  //   0b0101 - SHL
  //   0b0110 - SHR
  //   0b0111 - CNT
  //   0b1000 - CMPEQ
  //   0b1001 - CMPNEQ
  //   0b1010 - CMPLT
  //   0b1011 - CMPGT
  //   0b1100 - NOT
  //   0b1101 - AND
  //   0b1110 - OR
  //   0b1111 - XOR
endmodule
