// Logisim project CPU2.circ as structural Verilog: 1 circuit, main circuit main
module main (
);

  wire ALU_A_RIGHT_ZERO, ALU_A_SIGNED, ALU_A_WRITE, and_1_out, and_2_out, big_rom_1_p1, big_rom_1_p2, CLK,
       comparator_1_eq, HALT, JMP, JMPIF, JMPIFN, not_1_out, or_1_out, PAYLOAD_BYTE_WRITE,
       PAYLOAD_TINY_WRITE, PROG_JUMP, PROG_NEXT, PROG_REG_WRITE, pull_resistor_2_node, pull_resistor_3_node,
       REG_JUMP, register_bank_1_p12, SAVE_IR;
  wire [1:0] ALU_A_LEFT_ADDR_FIELD, ALU_A_OP_FIELD, ALU_A_OUTPUT_ADDR_FIELD, ALU_A_RIGHT_ADDR_FIELD,
       PROG_REG_ADDR_FIELD, REG_JUMP_ADDR_FIELD;
  wire [4:0] ALU_A_LEFT_ADDR, ALU_A_OP, ALU_A_OUTPUT_ADDR, ALU_A_RIGHT_ADDR, PAYLOAD_REG_TINY_A_ADDR,
       PAYLOAD_REG_TINY_B_ADDR, PROG_REG_ADDR, REG_JUMP_ADDR;
  wire [7:0] counter_2_q, pull_resistor_4_node;
  wire [11:0] IR_q;
  wire [15:0] counter_1_q;
  wire [19:0] INSN_DATA;
  wire [31:0] ALU_A_LEFT, ALU_A_OUTPUT, ALU_A_RIGHT, controlled_buffer_2_out, JMP_ADDR, PAYLOAD_REG_BYTE,
       PAYLOAD_REG_TINY_A, PAYLOAD_REG_TINY_B, PROG_VALUE, pull_resistor_1_node;

  Pull_Resistor pull_resistor_1 (.node(pull_resistor_1_node));
  Clock clock_1 (.out(CLK));
  Comparator #(.width(32), .mode("unsigned")) comparator_1 (
    .a(pull_resistor_1_node), .b(ALU_A_OUTPUT), .eq(comparator_1_eq));  // open: gt, lt
  and and_1 (and_1_out, JMPIFN, comparator_1_eq);
  and and_2 (and_2_out, ~comparator_1_eq, JMPIF);  // AND_Gate
  or or_1 (or_1_out, and_1_out, and_2_out, JMP);
  ROM #(.addrWidth(16), .dataWidth(32)) PROG (.addr(counter_1_q), .data(PROG_VALUE));
  Counter #(.width(16), .max('hffff)) counter_1 (
    .load(or_1_out), .up(pull_resistor_2_node), .count(PROG_NEXT), .clk(CLK), .Q(counter_1_q));  // open: clr, D, carry
  Pull_Resistor #(.pull(1)) pull_resistor_2 (.node(pull_resistor_2_node));
  // Mini_Bit_Selector #(.in_width(32), .out_width(16)) mini_bit_selector_1: pin names not known; wires that end beside it: JMP_ADDR
  Counter counter_2 (
    .load(SAVE_IR), .up(pull_resistor_3_node), .count(pull_resistor_3_node), .clk(CLK),
    .D(pull_resistor_4_node), .Q(counter_2_q));  // open: clr, carry
  Pull_Resistor #(.pull(1)) pull_resistor_3 (.node(pull_resistor_3_node));
  Pull_Resistor pull_resistor_4 (.node(pull_resistor_4_node));
  Register #(.width(32)) IR (.D(PROG_VALUE), .en(SAVE_IR), .clk(CLK), .Q({IR_q, INSN_DATA}));  // open: clr
  assign JMP_ADDR = PROG_JUMP ? PROG_VALUE : 32'bz;  // Controlled_Buffer controlled_buffer_1
  // Big_ROM #(.addressWidth(20), .valueWidth(64)) big_rom_1: pin names not known; wires that end beside it: big_rom_1_p1, big_rom_1_p2
  // Splitter #(.fanout(32), .incoming(32), .appear("right"), .spacing("double")) splitter_1: pin names not known; wires that end beside it: big_rom_1_p1, HALT, SAVE_IR
  // Splitter #(.appear("center"), .spacing("double")) splitter_2: pin names not known; wires that end beside it: PROG_NEXT, PROG_REG_WRITE, PROG_REG_ADDR_FIELD
  // Splitter #(.appear("center"), .spacing("double")) splitter_3: pin names not known; wires that end beside it: ALU_A_LEFT_ADDR_FIELD
  // Splitter #(.appear("center"), .spacing("double")) splitter_4: pin names not known; wires that end beside it: ALU_A_RIGHT_ADDR_FIELD
  // Splitter #(.appear("center"), .spacing("double")) splitter_5: pin names not known; wires that end beside it: ALU_A_OUTPUT_ADDR_FIELD
  // Splitter #(.appear("center"), .spacing("double")) splitter_6: pin names not known; wires that end beside it: ALU_A_SIGNED, ALU_A_WRITE, JMP, ALU_A_OP_FIELD
  // Splitter #(.appear("center"), .spacing("double")) splitter_7: pin names not known; wires that end beside it: PROG_JUMP, REG_JUMP, PAYLOAD_BYTE_WRITE, PAYLOAD_TINY_WRITE, JMPIF, JMPIFN, ALU_A_RIGHT_ZERO, REG_JUMP_ADDR_FIELD
  // Splitter #(.fanout(32), .incoming(32), .appear("right"), .spacing("double")) splitter_8: pin names not known; wires that end beside it: big_rom_1_p2
  not not_1 (not_1_out, ALU_A_RIGHT_ZERO);
  assign controlled_buffer_2_out = not_1_out ? ALU_A_RIGHT : 32'bz;  // Controlled_Buffer controlled_buffer_2
  Pull_Resistor pull_resistor_5 (.node(controlled_buffer_2_out));
  // ALU #(.width(32)) alu_1: pin names not known; wires that end beside it: ALU_A_SIGNED, ALU_A_OP, ALU_A_LEFT, controlled_buffer_2_out, ALU_A_OUTPUT
  Multiplexer #(.select(2), .width(5), .enable("false")) multiplexer_1 (
    .in0(INSN_DATA[4:0]), .in1(INSN_DATA[9:5]), .in2(INSN_DATA[14:10]), .in3(INSN_DATA[19:15]),
    .out(PROG_REG_ADDR), .sel(PROG_REG_ADDR_FIELD));
  Multiplexer #(.select(2), .width(5), .enable("false")) multiplexer_2 (
    .in0(INSN_DATA[4:0]), .in1(INSN_DATA[9:5]), .in2(INSN_DATA[14:10]), .in3(INSN_DATA[19:15]),
    .out(ALU_A_LEFT_ADDR), .sel(ALU_A_LEFT_ADDR_FIELD));
  Multiplexer #(.select(2), .width(5), .enable("false")) multiplexer_3 (
    .in0(INSN_DATA[4:0]), .in1(INSN_DATA[9:5]), .in2(INSN_DATA[14:10]), .in3(INSN_DATA[19:15]),
    .out(ALU_A_RIGHT_ADDR), .sel(ALU_A_RIGHT_ADDR_FIELD));
  Multiplexer #(.select(2), .width(5), .enable("false")) multiplexer_4 (
    .in0(INSN_DATA[4:0]), .in1(INSN_DATA[9:5]), .in2(INSN_DATA[14:10]), .in3(INSN_DATA[19:15]),
    .out(ALU_A_OUTPUT_ADDR), .sel(ALU_A_OUTPUT_ADDR_FIELD));
  Multiplexer #(.select(2), .width(5), .enable("false")) multiplexer_5 (
    .in0(INSN_DATA[4:0]), .in1(INSN_DATA[9:5]), .in2(INSN_DATA[14:10]), .in3(INSN_DATA[19:15]),
    .out(ALU_A_OP), .sel(ALU_A_OP_FIELD));
  Multiplexer #(.select(2), .width(5), .enable("false")) multiplexer_6 (
    .in0(INSN_DATA[4:0]), .in1(INSN_DATA[9:5]), .in2(INSN_DATA[14:10]), .in3(INSN_DATA[19:15]),
    .out(REG_JUMP_ADDR), .sel(REG_JUMP_ADDR_FIELD));
  Multiplexer #(.select(2), .width(5), .enable("false")) multiplexer_7 (
    .in0(INSN_DATA[4:0]), .in1(INSN_DATA[9:5]), .in2(INSN_DATA[14:10]), .in3(INSN_DATA[19:15]),
    .out(REG_JUMP_ADDR), .sel(REG_JUMP_ADDR_FIELD));
  Multiplexer #(.select(2), .width(5), .enable("false")) multiplexer_8 (
    .in0(INSN_DATA[4:0]), .in1(INSN_DATA[9:5]), .in2(INSN_DATA[14:10]), .in3(INSN_DATA[19:15]),
    .out(REG_JUMP_ADDR), .sel(REG_JUMP_ADDR_FIELD));
  // Mini_Bit_Extender #(.out_width(32)) mini_bit_extender_1: pin names not known; wires that end beside it: INSN_DATA[7:0], PAYLOAD_REG_BYTE
  // Mini_Bit_Extender #(.in_width(5), .out_width(32)) mini_bit_extender_2: pin names not known; wires that end beside it: PAYLOAD_REG_TINY_B
  // Mini_Bit_Extender #(.in_width(5), .out_width(32)) mini_bit_extender_3: pin names not known; wires that end beside it: PAYLOAD_REG_TINY_A
  // Splitter #(.fanout(4), .incoming(20), .appear("center"), .spacing("double"), .bit1(0), .bit2(0), .bit3(0), .bit4(0), .bit5(1), .bit6(1), .bit7(1), .bit8(1), .bit9(1), .bit10(2), .bit11(2), .bit12(2), .bit13(2), .bit14(2), .bit15(3), .bit16(3), .bit17(3), .bit18(3), .bit19(3)) splitter_9: pin names not known; wires that end beside it: INSN_DATA, PAYLOAD_REG_TINY_B_ADDR, PAYLOAD_REG_TINY_A_ADDR
  // Register_Bank #(.width(32), .registerCount(32), .portCount(32)) register_bank_1: pin names not known; wires that end beside it: REG_JUMP_ADDR, ALU_A_OUTPUT_ADDR, ALU_A_RIGHT_ADDR, ALU_A_LEFT_ADDR, PROG_REG_ADDR, CLK, PAYLOAD_REG_BYTE, ALU_A_WRITE, ALU_A_OUTPUT, PROG_REG_WRITE, PROG_VALUE, register_bank_1_p12, REG_JUMP, JMP_ADDR, ALU_A_RIGHT, ALU_A_LEFT
  // Probe on register_bank_1_p12

  // Other names for the same wires on the sheet: PAYLOAD_REG_BYTE_ADDR[4:0] = INSN_DATA[19:15]

  // Notes on the sheet:
  //   contents of PROG (hex, n*v repeats v):
  //   200001 355022 400140 208001 400541 420023 790c80 a 600000 4 790020 e 600000 2 400082 600000 2
endmodule
